# Fritzing sketch GamesCase1 (saved by Fritzing 0.7.11b)
breadboards: 1

parts:
  U1 = atmega328 [package=dip]
  C4 = Ceramic Capacitor [capacitance=100nF package="200 mil [THT, multilayer]"]
  C5 = Ceramic Capacitor [capacitance=22µF package="200 mil [THT, multilayer]"]
  C6 = Ceramic Capacitor [capacitance=22µF package="200 mil [THT, multilayer]"]
  R1 = 10k Ω Resistor [package=THT]
  XTAL1 = Crystal [frequency="16 Mhz" package=THT]
  J1 = double row male pin header, 2 pins [form="♂ (male)"]  # not connected
  J3 = double row male pin header, 2 pins [form="♂ (male)"]
  M1 = DC Motor
  J4 = Basic Servo
  LED1 = LED - 3mm [color="Red (633nm)" package="3 mm [THT]"]
  LED2 = green smd LED [package="1206 [SMD]"]
  IC1 = L293D [package=THT]
  R4 = Rotary Potentiometer (Large) [maximum_resistance=100kΩ package=THT]
  J5 = Generic male header - 7 pins [package=THT]  # not connected
  S1 = Pushbutton [package=THT]  # not connected
  S2 = Pushbutton [package=THT]  # not connected
  R7 = Resistor [tolerance=±5% resistance=10k package=THT]  # not connected
  R3 = 470 Ω Resistor [package=THT]
  R2 = 470 Ω Resistor [package=THT]
  R8 = Resistor [tolerance=±5% resistance=10k package=THT]  # not connected
  R9 = Resistor [tolerance=±5% resistance=10k package=THT]  # not connected

nets:
  N1: U1.RESET, U1.D0_(RX), C4.1, R1.Pin_0, J3.pin2
  N2: U1.D1_(TX), J3.pin1
  N3: U1.D2, IC1.In_1
  N4: U1.D3_(PWM), IC1.In_2
  VCC: U1.D4, U1.VCC, U1.AVCC, R1.Pin_1, J4.vcc, IC1.+Vmotor, IC1.+V, R4.leg2
  GND: U1.GND, C5.0, C6.0, J4.gnd, LED1.cathode, LED2.cathode, IC1.0V, R4.leg1
  N5: U1.XLAT1, C6.1, XTAL1.pin_1
  N6: U1.XLAT2, C5.1, XTAL1.pin_0
  N7: U1.D9_(PWM), LED2.anode, IC1.Enable_1, R2.Pin_1
  N8: U1.D11_(PWM), J4.pulse
  N9: U1.D12, R3.Pin_0
  N10: U1.D13, R2.Pin_0
  N11: U1.A5, R4.wiper
  N12: M1.pin_1, IC1.Out_2_(_Controlled_by_Enable_1_)
  N13: M1.pin_2, IC1.Out_1_(_Controlled_by_Enable_1_)
  N14: LED1.anode, R3.Pin_1

notes:
  add pull down resistor and fly leads for position sensor and stop
