# Fritzing sketch safe (saved by Fritzing 0.7.11b)
breadboards: 1

parts:
  U1 = atmega328 [package=dip]
  C4 = Ceramic Capacitor [capacitance=100nF package="200 mil [THT, multilayer]"]
  C5 = Ceramic Capacitor [capacitance=22µF package="200 mil [THT, multilayer]"]
  C6 = Ceramic Capacitor [capacitance=22µF package="200 mil [THT, multilayer]"]
  R1 = 10k Ω Resistor [package=THT]
  XTAL1 = Crystal [frequency="16 Mhz" package=THT]
  J1 = double row male pin header, 2 pins [form="♂ (male)"]  # not connected
  J3 = double row male pin header, 2 pins [form="♂ (male)"]
  U2 = Mystery Part - 7 pins [package=THT]
  R2 = Resistor [tolerance=±5% resistance=10k package=THT]
  R3 = Resistor [tolerance=±5% resistance=10k package=THT]
  R4 = Resistor [tolerance=±5% resistance=10k package=THT]
  LED1 = green smd LED [package="1206 [SMD]"]
  J4 = Basic Servo
  R5 = Resistor [tolerance=±5% resistance=220 package=THT]
  LED2 = red smd LED [package="1206 [SMD]"]  # not connected
  R6 = Resistor [tolerance=±5% resistance=220 package=THT]  # not connected

nets:
  N1: U1.RESET, U1.D0_(RX), C4.1, R1.Pin_0, J3.pin2
  N2: U1.D1_(TX), J3.pin1
  VCC: U1.D4, U1.VCC, U1.AVCC, R1.Pin_1, J4.vcc
  GND: U1.GND, C5.0, C6.0, LED1.cathode, J4.gnd
  N3: U1.XLAT1, C6.1, XTAL1.pin_1
  N4: U1.XLAT2, C5.1, XTAL1.pin_0
  N5: U1.D5_(PWM), J4.pulse
  N6: U1.D6_(PWM), R4.Pin_0
  N7: U1.D7, R3.Pin_0
  N8: U1.D8, R2.Pin_0
  N9: U1.D9_(PWM), U2.leg4
  N10: U1.D10_(PWM), U2.leg3
  N11: U1.D11_(PWM), U2.leg2
  N12: U1.D12, U2.leg1
  N13: U1.D13, R5.Pin_1
  N14: U2.leg5, R4.Pin_1
  N15: U2.leg6, R3.Pin_1
  N16: U2.leg7, R2.Pin_1
  N17: LED1.anode, R5.Pin_0
