# Fritzing sketch tom-trebuchet (saved by Fritzing 0.7.11b)
breadboards: 1

parts:
  U1 = atmega328 [package=dip]
  C4 = Ceramic Capacitor [capacitance=100nF package="200 mil [THT, multilayer]"]
  C5 = Ceramic Capacitor [capacitance=22µF package="200 mil [THT, multilayer]"]
  C6 = Ceramic Capacitor [capacitance=22µF package="200 mil [THT, multilayer]"]
  R1 = 10k Ω Resistor [package=THT]
  XTAL1 = Crystal [frequency="16 Mhz" package=THT]
  J1 = double row male pin header, 2 pins [form="♂ (male)"]  # not connected
  J3 = double row male pin header, 2 pins [form="♂ (male)"]
  J4 = Infrared Proximity Sensor
  R2 = 470 Ω Resistor [package=THT]  # not connected
  R3 = Photocell (LDR) [package=THT]  # not connected
  J5 = Basic Servo
  S1 = Pushbutton [package="[THT]"]  # not connected
  LED1 = Blue smd LED [package="0603 [SMD]"]  # not connected
  R4 = Resistor [tolerance=±5% resistance=10k package=THT]  # not connected

nets:
  N1: U1.RESET, U1.D0_(RX), C4.1, R1.Pin_0, J3.pin2
  N2: U1.D1_(TX), J3.pin1
  N3: U1.D4, U1.VCC, U1.AVCC, R1.Pin_1
  N4: U1.GND, C5.0, C6.0
  N5: U1.XLAT1, C6.1, XTAL1.pin_1
  N6: U1.XLAT2, C5.1, XTAL1.pin_0
  N7: U1.D9_(PWM), J5.pulse
  N8: U1.A5, J4.Vout
  GND: J4.GND, J5.gnd
  VCC: J4.Vcc, J5.vcc
